# Fritzing sketch circuit (saved by Fritzing 1.0.2b)

parts:
  WeMos_D1_Mini1 = WeMos D1 Mini
  Part1 = BME280 Breakout
  U2 = Sharp Dust Sensor [part_number=GP2Y1010AU0F]
  F1 = Fan - Ventilador [package=THT]
  U1 = Ikea Vindriktning [package="SIP (Single Inline) [THT]"]

nets:
  3V3: WeMos_D1_Mini1.3V3, Part1.3.3V
  5V: WeMos_D1_Mini1.5V, U1.+5V
  N1: WeMos_D1_Mini1.D1, Part1.SCK/SCL
  N2: WeMos_D1_Mini1.D2, Part1.SDI/SDA
  N3: WeMos_D1_Mini1.D5, U1.REST
  GND: WeMos_D1_Mini1.G, Part1.GND, U1.GND
  N4: U2.V-LED, U1.dust4
  N5: U2.LED-GND, U1.dust3
  N6: U2.LED, U1.dust2
  N7: U2.S-GND, U1.dust1
  N8: F1.5V, U1.fan+
  N9: F1.GND, U1.fan-

notes:
  USB-C Power

custom parts:
  WeMos D1 Mini: The D1 mini is a mini wifi board based on ESP-8266EX.
  Sharp Dust Sensor: Sharp GP2Y1010AU0F Dust Sensor
  Fan - Ventilador: Ventilador de 2 pines, se encuentra comunmente en computadoras de escritorio
  Ikea Vindriktning: vindriktning dust sensor IC
